# Fritzing sketch C86_Circuit (saved by Fritzing 0.9.0b)
breadboards: 1

parts:
  R4 = Resistor [tolerance=±5% resistance=4.7k package=THT]
  R5 = Resistor [tolerance=±5% resistance=4.7k package=THT]
  C3 = Ceramic Capacitor [capacitance=100nF package="100 mil [THT, multilayer]"]
  R6 = Resistor [tolerance=±5% resistance=1k package=THT]
  C4 = Ceramic Capacitor [capacitance=47nF package="100 mil [THT, multilayer]"]
  パーツ4 = Audio Jack Breakout
  パーツ6 = Arduino Mega ADK (Rev3)
  IC2 = IC, DIP package, 28 pins [chip_label="AquesTalk ATP3011F4"]

nets:
  N1: R4.Pin_1, R5.Pin_1, C3.0, パーツ6.IOREF, パーツ6.5V, IC2.pin7, IC2.pin20
  N2: R5.Pin_0, パーツ6.D20/SDA, IC2.pin27
  GND: C3.1, C4.0, パーツ4.GND, パーツ6.GND, IC2.pin4, IC2.pin8, IC2.pin22
  N3: R6.Pin_0, IC2.pin12
  N4: R6.Pin_1, C4.1, パーツ4.TIP
  N5: パーツ6.D21/SCL, IC2.pin28
  N6: パーツ6.RESET, IC2.pin1
